# Fritzing sketch counter (saved by Fritzing 0.9.3b)
breadboards: 1

parts:
  Part1 = Arduino Uno (Rev3)
  S1 = Pushbutton [package="[THT]"]
  S2 = Pushbutton [package="[THT]"]
  LED_N1 = LED - 5mm [color="Red (633nm)" package="5 mm [THT]"]
  LED_N2 = LED - 5mm [color="Red (633nm)" package="5 mm [THT]"]
  LED_Switch = LED - 5mm [color="Red (633nm)" package="5 mm [THT]"]
  R5 = 165 Ω Resistor [package=THT]
  R4 = 165 Ω Resistor [package=THT]
  R1 = 165 Ω Resistor [package=THT]
  R2 = 165 Ω Resistor [package=THT]
  R3 = 165 Ω Resistor [package=THT]

nets:
  N1: Part1.D9_PWM, LED_N1.anode
  N2: Part1.D11_PWM/MOSI, LED_N2.anode
  N3: Part1.D13/SCK, LED_Switch.anode
  N4: Part1.GND, R5.Pin_0, R4.Pin_0, R1.Pin_0, R2.Pin_0, R3.Pin_0
  N5: Part1.D2, S1.Pin_3, S1.Pin_4, R4.Pin_1
  N6: Part1.D6_PWM, S2.Pin_3, S2.Pin_4, R5.Pin_1
  N7: Part1.5V, S1.Pin_1, S1.Pin_2, S2.Pin_1, S2.Pin_2
  N8: LED_N1.cathode, R1.Pin_1
  N9: LED_N2.cathode, R2.Pin_1
  N10: LED_Switch.cathode, R3.Pin_1

custom parts:
  165 Ω Resistor: A generic resistor (0.25W)
